// Logisim project cpu_v1.circ as structural Verilog: 12 circuits, main circuit main
module main (
  input  in_1,
  input  in_2,
  input  in_3,
  input  in_4,
  input  in_5,
  input  in_6,
  input  in_7,
  input  PRG,
  input  in_9,
  input  in_10,
  input  in_11,
  input  in_12,
  input  in_13,
  input  in_14,
  input  in_15,
  input  INo
);

  wire CLK_out, not_1_out;
  wire [7:0] controlled_buffer_1_out, controlled_buffer_2_out, cpu_mar_1_q, cpu_out_1_q, cpu_pc_1_q,
       dipswitch_1_sw8, dipswitch_2_sw8;

  Clock CLK (.out(CLK_out));
  not not_1 (not_1_out, PRG);
  DotMatrix #(.matrixcols(8), .matrixrows(1)) dotmatrix_1 (
    .col0(cpu_mar_1_q[7]), .col1(cpu_mar_1_q[6]), .col2(cpu_mar_1_q[5]), .col3(cpu_mar_1_q[4]),
    .col4(cpu_mar_1_q[3]), .col5(cpu_mar_1_q[2]), .col6(cpu_mar_1_q[1]), .col7(cpu_mar_1_q[0]));
  DipSwitch dipswitch_1 (
    .sw1(dipswitch_1_sw8[7]), .sw2(dipswitch_1_sw8[6]), .sw3(dipswitch_1_sw8[5]), .sw4(dipswitch_1_sw8[4]),
    .sw5(dipswitch_1_sw8[3]), .sw6(dipswitch_1_sw8[2]), .sw7(dipswitch_1_sw8[1]), .sw8(dipswitch_1_sw8[0]));
  cpu_MAR cpu_mar_1 (.CLR(in_7), .CLK(CLK_out), .MARi(in_6), .D(cpu_pc_1_q), .MARo(in_5), .Q(cpu_mar_1_q));
  assign controlled_buffer_1_out = not_1_out ? cpu_mar_1_q : 8'bz;  // Controlled_Buffer controlled_buffer_1
  assign controlled_buffer_2_out = PRG ? cpu_mar_1_q : 8'bz;  // Controlled_Buffer controlled_buffer_2
  cpu_IR cpu_ir_1 (.CLR(in_15), .CLK(CLK_out), .IRi(in_14), .D(cpu_pc_1_q), .IRo(in_13));  // open: Q
  DotMatrix #(.matrixcols(8), .matrixrows(1)) dotmatrix_2 (
    .col0(cpu_pc_1_q[7]), .col1(cpu_pc_1_q[6]), .col2(cpu_pc_1_q[5]), .col3(cpu_pc_1_q[4]),
    .col4(cpu_pc_1_q[3]), .col5(cpu_pc_1_q[2]), .col6(cpu_pc_1_q[1]), .col7(cpu_pc_1_q[0]));
  cpu_PC cpu_pc_1 (.D(cpu_pc_1_q), .CLR(in_4), .CLK(CLK_out), .PCC(in_3), .PCi(in_2), .PCo(in_1), .Q(cpu_pc_1_q));
  cpu_RAM cpu_ram_1 (
    .D(cpu_pc_1_q), .CLK(CLK_out), .RAMo(in_10), .RAMi(in_9), .ADR(controlled_buffer_1_out), .Q(cpu_pc_1_q));
  cpu_ROM cpu_rom_1 (
    .D(dipswitch_1_sw8), .CLK(CLK_out), .ROMo(in_12), .ROMi(in_11), .ADR(controlled_buffer_2_out),
    .Q(cpu_pc_1_q));
  assign cpu_pc_1_q = INo ? dipswitch_2_sw8 : 8'bz;  // Controlled_Buffer controlled_buffer_3
  cpu_ALU cpu_alu_1 (.Q(cpu_pc_1_q));  // open: X, Y, MODE, ALUo, F
  cpu_A cpu_a_1 ();  // open: CLR, CLK, Ai, D, Ao, Q
  cpu_B cpu_b_1 ();  // open: CLR, CLK, Bi, D, Bo, Q
  cpu_OUT cpu_out_1 (.Q(cpu_out_1_q), .D(cpu_pc_1_q));  // open: CLR, CLK, OUTi
  DipSwitch dipswitch_2 (
    .sw1(dipswitch_2_sw8[7]), .sw2(dipswitch_2_sw8[6]), .sw3(dipswitch_2_sw8[5]), .sw4(dipswitch_2_sw8[4]),
    .sw5(dipswitch_2_sw8[3]), .sw6(dipswitch_2_sw8[2]), .sw7(dipswitch_2_sw8[1]), .sw8(dipswitch_2_sw8[0]));
  cpu_C cpu_c_1 ();  // open: CLR, CLK, Ci, D, Co, Q
  cpu_D cpu_d_1 ();  // open: CLR, CLK, Di, D, Do, Q
  DotMatrix #(.matrixcols(8), .matrixrows(1)) dotmatrix_3 (
    .col0(cpu_out_1_q[7]), .col1(cpu_out_1_q[6]), .col2(cpu_out_1_q[5]), .col3(cpu_out_1_q[4]),
    .col4(cpu_out_1_q[3]), .col5(cpu_out_1_q[2]), .col6(cpu_out_1_q[1]), .col7(cpu_out_1_q[0]));
endmodule

module cpu_PC (
  input  PCo,
  input  PCi,
  input  PCC,
  input  CLK,
  input  CLR,
  input  [7:0] D,
  output [7:0] Q
);

  wire controlled_buffer_1_out, or_1_out;
  wire [7:0] counter_1_q;

  or or_1 (or_1_out, PCi, PCC);
  assign controlled_buffer_1_out = or_1_out ? CLK : 1'bz;  // Controlled_Buffer controlled_buffer_1
  Counter counter_1 (
    .clr(CLR), .load(PCi), .clk(controlled_buffer_1_out), .Q(counter_1_q));  // open: up, count, D, carry
  assign Q = PCo ? counter_1_q : 8'bz;  // Controlled_Buffer controlled_buffer_2
endmodule

module cpu_RAM (
  input  [7:0] ADR,
  input  RAMi,
  input  RAMo,
  input  CLK,
  input  [7:0] D,
  output [7:0] Q
);

  wire [7:0] ram_1_dout;

  RAM #(.databus("bibus")) ram_1 (.addr(ADR), .we(RAMi), .oe(RAMo), .clk(CLK), .din(D), .dout(ram_1_dout));
  assign Q = RAMo ? ram_1_dout : 8'bz;  // Controlled_Buffer controlled_buffer_1
endmodule

module cpu_MAR (
  input  MARo,
  input  [7:0] D,
  input  MARi,
  input  CLK,
  input  CLR,
  output [7:0] Q
);

  wire [7:0] register_1_q;

  Register register_1 (.D(D), .en(MARi), .clk(CLK), .Q(register_1_q), .clr(CLR));
  assign Q = MARo ? register_1_q : 8'bz;  // Controlled_Buffer controlled_buffer_1
endmodule

module cpu_ROM (
  input  [7:0] ADR,
  input  ROMi,
  input  ROMo,
  input  CLK,
  input  [7:0] D,
  output [7:0] Q
);

  wire [7:0] ram_1_dout;

  RAM #(.databus("bibus")) ram_1 (.addr(ADR), .we(ROMi), .oe(ROMo), .clk(CLK), .din(D), .dout(ram_1_dout));
  assign Q = ROMo ? ram_1_dout : 8'bz;  // Controlled_Buffer controlled_buffer_1
endmodule

module cpu_IR (
  input  IRo,
  input  [7:0] D,
  input  IRi,
  input  CLK,
  input  CLR,
  output [7:0] Q
);

  wire [7:0] register_1_q;

  Register register_1 (.D(D), .en(IRi), .clk(CLK), .Q(register_1_q), .clr(CLR));
  assign Q = IRo ? register_1_q : 8'bz;  // Controlled_Buffer controlled_buffer_1
endmodule

module cpu_A (
  input  Ao,
  input  [7:0] D,
  input  Ai,
  input  CLK,
  input  CLR,
  output [7:0] Q
);

  wire [7:0] register_1_q;

  Register register_1 (.D(D), .en(Ai), .clk(CLK), .Q(register_1_q), .clr(CLR));
  assign Q = Ao ? register_1_q : 8'bz;  // Controlled_Buffer controlled_buffer_1
endmodule

module cpu_B (
  input  Bo,
  input  [7:0] D,
  input  Bi,
  input  CLK,
  input  CLR,
  output [7:0] Q
);

  wire [7:0] register_1_q;

  Register register_1 (.D(D), .en(Bi), .clk(CLK), .Q(register_1_q), .clr(CLR));
  assign Q = Bo ? register_1_q : 8'bz;  // Controlled_Buffer controlled_buffer_1
endmodule

module cpu_C (
  input  Co,
  input  [7:0] D,
  input  Ci,
  input  CLK,
  input  CLR,
  output [7:0] Q
);

  wire [7:0] register_1_q;

  Register register_1 (.D(D), .en(Ci), .clk(CLK), .Q(register_1_q), .clr(CLR));
  assign Q = Co ? register_1_q : 8'bz;  // Controlled_Buffer controlled_buffer_1
endmodule

module cpu_D (
  input  Do,
  input  [7:0] D,
  input  Di,
  input  CLK,
  input  CLR,
  output [7:0] Q
);

  wire [7:0] register_1_q;

  Register register_1 (.D(D), .en(Di), .clk(CLK), .Q(register_1_q), .clr(CLR));
  assign Q = Do ? register_1_q : 8'bz;  // Controlled_Buffer controlled_buffer_1
endmodule

module cpu_OUT (
  input  [7:0] D,
  input  OUTi,
  input  CLK,
  input  CLR,
  output [7:0] Q
);

  Register register_1 (.D(D), .en(OUTi), .clk(CLK), .Q(Q), .clr(CLR));
endmodule

module cpu_ALU (
  input  [2:0] MODE,
  input  ALUo,
  input  [7:0] X,
  input  [7:0] Y,
  output [7:0] Q,
  output [3:0] F
);

  wire adder_1_cout, adder_2_cout, subtractor_1_bout, subtractor_2_bout, xnor_1_out, xor_2_out;
  wire [6:0] multiplexer_1_out;
  wire [7:0] adder_1_out, adder_2_out, and_1_out, or_1_out, subtractor_1_out, subtractor_2_out, xor_1_out;

  assign and_1_out = X & Y;  // AND_Gate and_1, 8 bits wide
  assign or_1_out = X | Y;  // OR_Gate or_1, 8 bits wide
  assign xor_1_out = X ^ Y;  // XOR_Gate xor_1, 8 bits wide
  Adder adder_1 (.a(X), .b(Y), .out(adder_1_out), .cout(adder_1_cout));  // open: cin
  Subtractor subtractor_1 (.a(X), .b(Y), .out(subtractor_1_out), .bout(subtractor_1_bout));  // open: bin
  Adder adder_2 (.a(X), .b(Y), .out(adder_2_out), .cin(1'b1), .cout(adder_2_cout));
  Subtractor subtractor_2 (.a(X), .b(Y), .out(subtractor_2_out), .bin(1'b1), .bout(subtractor_2_bout));
  Multiplexer #(.select(3), .width(8), .enable("false")) multiplexer_1 (
    .in0(adder_1_out), .in1(subtractor_1_out), .in2(adder_2_out), .in3(subtractor_2_out), .in4(and_1_out),
    .in5(or_1_out), .in6(xor_1_out), .out({F[2], multiplexer_1_out}), .sel(MODE));  // open: in7
  Multiplexer #(.select(2), .enable("false")) multiplexer_2 (
    .in0(adder_1_cout), .in1(subtractor_1_bout), .in2(adder_2_cout), .in3(subtractor_2_bout), .out(F[0]),
    .sel(MODE[1:0]));
  xor xor_2 (xor_2_out, X[7], F[2]);
  xnor xnor_1 (xnor_1_out, X[7], Y[7]);
  nor nor_1 (F[3], F[2], multiplexer_1_out[6], multiplexer_1_out[5], multiplexer_1_out[4], multiplexer_1_out[3], multiplexer_1_out[2], multiplexer_1_out[1], multiplexer_1_out[0]);
  and and_2 (F[1], xor_2_out, xnor_1_out);
  assign Q = ALUo ? {F[2], multiplexer_1_out} : 8'bz;  // Controlled_Buffer controlled_buffer_1
endmodule
